# Fritzing sketch meteo (saved by Fritzing 0.9.2b)
circuit board: 13.5108cm x 5.45182cm
breadboards: 1

parts:
  Part2 = Arduino Pro Mini Atmega328
  7_Segment_4_Digit_Display1 = 7-segment-4-digit-common-cathode-display [part_number=CA56-12SRWA package=7-segment-4digit-cathode]  # not connected
  U1 = A23 battery [package=battery-a23]
  DHT1 = DHT22 Humidity and Temperature Sensor
  S1 = Tilt Switch [package=THT]

nets:
  N1: Part2.A6, S1.Pin_1
  N2: Part2.A7, DHT1.DATA
  N3: Part2.GND#24, U1.-1, U1.-2
  N4: Part2.RAW, U1.+1, U1.+2
  VCC: Part2.VCC, DHT1.VDD
  N5: Part2.GND#45, DHT1.GND, S1.Pin_2

custom parts:
  Arduino Pro Mini Atmega328: Arduino Pro Mini based on Atmega328. This is a 5V Arduino running the 16MHz bootloader. There is a voltage regulator on board so it can accept voltage up to 12VDC. If you're supplying unregulated power to the board, be sure to connect to the "RAW" pin on not VCC.
  7-segment-4-digit-common-cathode-display: A 7 Segment 4 Digit common cathode display, with decimal points
  A23 battery: A23 battery (Duracell MN21 and Keystone holders No82)
